# Fritzing sketch R2D2 (saved by Fritzing 0.9.5d)

parts:
  SP1 = SPEAKER [package=pcb_mount_speaker]
  Part1 = 16-Channel 12-bit PWM Servo Driver - I2C [part_number=815]
  Part2 = Adafruit MAX98357A I2S 3W Class D Amplifier [part_number="Adafruit #3006"]
  MCU1 = Raspberry Pi Zero
  BATT1 = 4xAA Switchable Battery Pack w/Bare Wire
  J6 = Basic Servo
  J7 = Basic Servo
  J8 = Basic Servo

nets:
  N1: SP1.+, Part2.VO-
  N2: SP1.-, Part2.VO+
  N3: Part1.PWRIN, BATT1.POS
  GND: Part1.GND, Part2.GND, MCU1.pin_9, MCU1.pin_20, MCU1.pin_39, BATT1.NEG, J6.gnd, J7.gnd, J8.gnd
  N4: Part1.PWM2, J8.pulse
  VCC: Part1.5.0V, J6.vcc, J7.vcc, J8.vcc
  N5: Part1.PWM1, J6.pulse
  N6: Part1.PWM0, J7.pulse
  N7: Part1.VCC, MCU1.pin_1, MCU1.pin_17
  N8: Part1.SDA, MCU1.pin_3
  N9: Part1.SCL, MCU1.pin_5
  N10: Part2.VIN, MCU1.pin_2, MCU1.pin_4
  N11: Part2.DIN, MCU1.pin_40
  N12: Part2.BCLK, MCU1.pin_12
  N13: Part2.LRCLK, MCU1.pin_35

custom parts:
  16-Channel 12-bit PWM Servo Driver - I2C: You want to make a cool robot, maybe a hexapod walker, or maybe just a piece of art with a lot of moving parts. Or maybe you want to drive a lot of LEDs with precise PWM output. Using only two pins, control 16 free-running PWM outputs! You can even chain up 62 breakouts to control up to 992 PWM outputs.
  Adafruit MAX98357A I2S 3W Class D Amplifier: Listen to this good news - we now have an all in one digital audio amp breakout board that works incredibly well with the Raspberry Pi! If you're looking for an easy and low cost way to get you digital sound files bumpin' then the MAX08357 I2S Amp Breakout is for you. It takes standard I2S digital audio input and, not only decodes it into analog, but also amplifies it directly into a speaker.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
  4xAA Switchable Battery Pack w/Bare Wire: 4xAA Switchable Battery Pack with Bare Wire connection
